# Fritzing sketch rama_bread (saved by Fritzing 0.9.3b)
breadboards: 1

parts:
  KIT_XMC11_BOOT_1 = Boot Kit XMC1100 [part_number=KITXMC11BOOT001TOBO1]
  J1 = RJ11 Jack [package=rj11-6]  # not connected
  J2 = RJ11 Jack [package=rj11-6]  # not connected
  J3 = RJ11 Jack [package=rj11-6]  # not connected
  SJ1 = Solder Jumper [package=sj_2]
  BAT1 = BC9VPC [package=bc9vpc]
  R1 = Resistor [tolerance=±5% resistance=220 package="1206 [SMD]"]
  U1 = Voltage Regulator - 5V [package="DPak [SMD]"]
  LED1 = smd LED [color="Red (633nm)" package="1206 [SMD]"]
  Bauteil1 = Bluetooth HC-05 Macho

nets:
  N1: KIT_XMC11_BOOT_1.P1.2, Bauteil1.RXD
  N2: KIT_XMC11_BOOT_1.P1.3, Bauteil1.TXD
  GND: KIT_XMC11_BOOT_1.GND, BAT1.V-, U1.GND, LED1.anode, Bauteil1.GND
  N3: KIT_XMC11_BOOT_1.+3V3_DEV, Bauteil1.VCC
  N4: KIT_XMC11_BOOT_1.+5V_DEV, SJ1.2
  N5: SJ1.1, U1.output_voltage
  N6: BAT1.V+, R1.Pin_1, U1.input_voltage
  N7: R1.Pin_0, LED1.cathode

custom parts:
  Boot Kit XMC1100: The XMC1100 CPU Card for Arduino TM has two rows of pin headers which fully compatible with Arduino TM shield. Hence, user can buy various Arduino shield boards off - the - shelf to test the capabilities of XMC1100 Microcontroller. Summary of Features: XMC1100 Microcontroller in TSSOP-38 with 64 KB Flash and full peripheral set of XMC1100 series Detachable SEGGER J-Link Board shape & power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
